// Logisim project Computer.circ as structural Verilog
module cpu_core (
  input  reset,
  input  valid_curr,
  input  flush,
  input  stall
);

  wire and_1_out, CLK, ex_mem_register_1_branch_taken_out, ex_mem_register_1_memread_out,
       ex_mem_register_1_memwrite_out, ex_mem_register_1_regwrite_out, ex_mem_register_1_valid_out,
       execute_1_branch_taken, id_ex_register_1_alusrc_out, id_ex_register_1_alusrca_out,
       id_ex_register_1_branch_out, id_ex_register_1_i_tyep_jalr_out, id_ex_register_1_j_type_jal_out,
       id_ex_register_1_jump_out, id_ex_register_1_memread_out, id_ex_register_1_memwrite_out,
       id_ex_register_1_regwrite_out, id_ex_register_1_valid_out, if_id_register_1_valid_bit_out,
       instruction_decode_1_alusrc, instruction_decode_1_alusrca, instruction_decode_1_branch,
       instruction_decode_1_i_type_jalr, instruction_decode_1_j_type_jal, instruction_decode_1_jump,
       instruction_decode_1_memread, instruction_decode_1_memwrite, instruction_decode_1_regwrite,
       mem_wb_register_1_regwrite_out, mem_wb_register_1_valid_out, pc_control_unit_1_take_control_flow;
  wire [1:0] id_ex_register_1_aluop_out, instruction_decode_1_aluop;
  wire [2:0] ex_mem_register_1_writebacksel_out, id_ex_register_1_func3_out, id_ex_register_1_immsel_out,
       id_ex_register_1_writebacksel_out, instruction_decode_1_func3, instruction_decode_1_immsel,
       instruction_decode_1_writebacksel, mem_wb_register_1_writebacksel_out;
  wire [4:0] ex_mem_register_1_rd_out, id_ex_register_1_rd_out, id_ex_register_1_rs1_out,
       id_ex_register_1_rs2_out, instruction_decode_1_rd, instruction_decode_1_rs1, instruction_decode_1_rs2,
       mem_wb_register_1_rd_out;
  wire [6:0] id_ex_register_1_func7_out, instruction_decode_1_func7;
  wire [31:0] data_memory_subsystem_1_read_data, ex_mem_register_1_alu_result_out,
       ex_mem_register_1_immediate_out, ex_mem_register_1_pc_out, ex_mem_register_1_pc_target_address_out,
       ex_mem_register_1_rs2_data_out, execute_1_alu_result, execute_1_pc_target_address,
       id_ex_register_1_immediate_out, id_ex_register_1_pc_out, id_ex_register_1_rs1_data_out,
       id_ex_register_1_rs2_data_out, if_id_register_1_inst_out, if_id_register_1_pc_out,
       instruction_decode_1_immediate, instruction_fetch_1_instruction, instruction_fetch_1_pc,
       instruction_fetch_1_pc_plus_4, mem_wb_register_1_alu_result_out, mem_wb_register_1_immediate_out,
       mem_wb_register_1_mem_read_data_out, mem_wb_register_1_pc_out,
       mem_wb_register_1_pc_target_address_out, multiplexer_1_out, register_file_subsystem_1_read_data_1,
       register_file_subsystem_1_read_data_2, writeback_1_writeback_data;

  Clock u_CLK (.out(CLK));
  Multiplexer #(.width(32)) multiplexer_1 (
    .in0(instruction_fetch_1_pc_plus_4), .in1(execute_1_pc_target_address), .out(multiplexer_1_out),
    .sel(pc_control_unit_1_take_control_flow));
  instruction_fetch instruction_fetch_1 (
    .CLK(CLK), .reset(reset), .next_pc(multiplexer_1_out), .PC(instruction_fetch_1_pc),
    .Instruction(instruction_fetch_1_instruction), .PC_plus_4(instruction_fetch_1_pc_plus_4));  // open: pc_write_enable_later
  if_id_register if_id_register_1 (
    .CLK(CLK), .reset(reset), .flush(flush), .stall(stall), .valid_bit_in(valid_curr),
    .inst_in(instruction_fetch_1_instruction), .PC_in(instruction_fetch_1_pc),
    .valid_bit_out(if_id_register_1_valid_bit_out), .inst_out(if_id_register_1_inst_out),
    .PC_out(if_id_register_1_pc_out));
  instruction_decode instruction_decode_1 (
    .valid(if_id_register_1_valid_bit_out), .INSTRUCTION(if_id_register_1_inst_out),
    .func3(instruction_decode_1_func3), .func7(instruction_decode_1_func7), .rd(instruction_decode_1_rd),
    .rs1(instruction_decode_1_rs1), .rs2(instruction_decode_1_rs2),
    .Immediate(instruction_decode_1_immediate), .ALUOp(instruction_decode_1_aluop),
    .RegWrite(instruction_decode_1_regwrite), .ImmSel(instruction_decode_1_immsel),
    .MemWrite(instruction_decode_1_memwrite), .MemRead(instruction_decode_1_memread),
    .Jump(instruction_decode_1_jump), .I_type_JALR(instruction_decode_1_i_type_jalr),
    .J_type_JAL(instruction_decode_1_j_type_jal), .Branch(instruction_decode_1_branch),
    .ALUSrc(instruction_decode_1_alusrc), .ALUSrcA(instruction_decode_1_alusrca),
    .WritebackSel(instruction_decode_1_writebacksel));
  and and_1 (and_1_out, mem_wb_register_1_regwrite_out, mem_wb_register_1_valid_out);
  register_file_subsystem register_file_subsystem_1 (
    .CLK(CLK), .RESET(reset), .ADDRESS_R_1(instruction_decode_1_rs1), .ADDRESS_R_2(instruction_decode_1_rs2),
    .ADDRESS_W_3(mem_wb_register_1_rd_out), .WRITE_ENABLE(and_1_out),
    .WRITE_DATA(writeback_1_writeback_data), .READ_DATA_1(register_file_subsystem_1_read_data_1),
    .READ_DATA_2(register_file_subsystem_1_read_data_2));
  id_ex_register id_ex_register_1 (
    .CLK(CLK), .reset(reset), .stall(stall), .flush(flush), .valid_in(if_id_register_1_valid_bit_out),
    .func3_in(instruction_decode_1_func3), .func7_in(instruction_decode_1_func7),
    .PC_in(if_id_register_1_pc_out), .rd_in(instruction_decode_1_rd), .rs1_in(instruction_decode_1_rs1),
    .rs2_in(instruction_decode_1_rs2), .immediate_in(instruction_decode_1_immediate),
    .ALUOp_in(instruction_decode_1_aluop), .RegWrite_in(instruction_decode_1_regwrite),
    .ImmSel_in(instruction_decode_1_immsel), .MemWrite_in(instruction_decode_1_memwrite),
    .MemRead_in(instruction_decode_1_memread), .Jump_in(instruction_decode_1_jump),
    .I_TYEP_JALR_in(instruction_decode_1_i_type_jalr), .J_TYPE_JAL_in(instruction_decode_1_j_type_jal),
    .Branch_in(instruction_decode_1_branch), .ALUSrc_in(instruction_decode_1_alusrc),
    .ALUSrcA_in(instruction_decode_1_alusrca), .WritebackSel_in(instruction_decode_1_writebacksel),
    .rs1_data_in(register_file_subsystem_1_read_data_1), .rs2_data_in(register_file_subsystem_1_read_data_2),
    .valid_out(id_ex_register_1_valid_out), .func3_out(id_ex_register_1_func3_out),
    .func7_out(id_ex_register_1_func7_out), .PC_out(id_ex_register_1_pc_out),
    .rd_out(id_ex_register_1_rd_out), .rs1_out(id_ex_register_1_rs1_out), .rs2_out(id_ex_register_1_rs2_out),
    .immediate_out(id_ex_register_1_immediate_out), .ALUOp_out(id_ex_register_1_aluop_out),
    .RegWrite_out(id_ex_register_1_regwrite_out), .ImmSel_out(id_ex_register_1_immsel_out),
    .MemWrite_out(id_ex_register_1_memwrite_out), .MemRead_out(id_ex_register_1_memread_out),
    .Jump_out(id_ex_register_1_jump_out), .I_TYEP_JALR_out(id_ex_register_1_i_tyep_jalr_out),
    .J_TYPE_JAL_out(id_ex_register_1_j_type_jal_out), .Branch_out(id_ex_register_1_branch_out),
    .ALUSrc_out(id_ex_register_1_alusrc_out), .ALUSrcA_out(id_ex_register_1_alusrca_out),
    .WritebackSel_out(id_ex_register_1_writebacksel_out), .rs1_data_out(id_ex_register_1_rs1_data_out),
    .rs2_data_out(id_ex_register_1_rs2_data_out));
  // NoConnect on id_ex_register_1_rs1_out
  // NoConnect on id_ex_register_1_rs2_out
  // NoConnect on id_ex_register_1_immsel_out
  // NoConnect on id_ex_register_1_jump_out
  execute execute_1 (
    .valid(id_ex_register_1_valid_out), .func3(id_ex_register_1_func3_out),
    .func7(id_ex_register_1_func7_out), .PC(id_ex_register_1_pc_out),
    .Immediate(id_ex_register_1_immediate_out), .ALUOp(id_ex_register_1_aluop_out),
    .ALUSrc(id_ex_register_1_alusrc_out), .ALUSrcA(id_ex_register_1_alusrca_out),
    .I_TYEP_JALR(id_ex_register_1_i_tyep_jalr_out), .rs1_data(id_ex_register_1_rs1_data_out),
    .rs2_data(id_ex_register_1_rs2_data_out), .pc_target_address(execute_1_pc_target_address),
    .ALU_Result(execute_1_alu_result), .branch_taken(execute_1_branch_taken));
  pc_control_unit pc_control_unit_1 (
    .branch_taken(execute_1_branch_taken), .I_TYPE_JALR(id_ex_register_1_i_tyep_jalr_out),
    .J_TYPE_JAL(id_ex_register_1_j_type_jal_out), .B_TYPE_BRANCH(id_ex_register_1_branch_out),
    .take_control_flow(pc_control_unit_1_take_control_flow));
  ex_mem_register ex_mem_register_1 (
    .CLK(CLK), .reset(reset), .stall(stall), .flush(flush), .valid_in(id_ex_register_1_valid_out),
    .pc_target_address_in(execute_1_pc_target_address), .ALU_Result_in(execute_1_alu_result),
    .branch_taken_in(execute_1_branch_taken), .rd_in(id_ex_register_1_rd_out),
    .PC_in(id_ex_register_1_pc_out), .immediate_in(id_ex_register_1_immediate_out),
    .RegWrite_in(id_ex_register_1_regwrite_out), .MemWrite_in(id_ex_register_1_memwrite_out),
    .MemRead_in(id_ex_register_1_memread_out), .WritebackSel_in(id_ex_register_1_writebacksel_out),
    .rs2_data_in(id_ex_register_1_rs2_data_out), .valid_out(ex_mem_register_1_valid_out),
    .pc_target_address_out(ex_mem_register_1_pc_target_address_out),
    .ALU_Result_out(ex_mem_register_1_alu_result_out), .branch_taken_out(ex_mem_register_1_branch_taken_out),
    .rd_out(ex_mem_register_1_rd_out), .PC_out(ex_mem_register_1_pc_out),
    .immediate_out(ex_mem_register_1_immediate_out), .RegWrite_out(ex_mem_register_1_regwrite_out),
    .MemWrite_out(ex_mem_register_1_memwrite_out), .MemRead_out(ex_mem_register_1_memread_out),
    .WritebackSel_out(ex_mem_register_1_writebacksel_out), .rs2_data_out(ex_mem_register_1_rs2_data_out));
  // NoConnect on ex_mem_register_1_branch_taken_out
  data_memory_subsystem data_memory_subsystem_1 (
    .CLK(CLK), .ADDRESS_CPU(ex_mem_register_1_alu_result_out), .WRITE_DATA(ex_mem_register_1_rs2_data_out),
    .MemWrite(ex_mem_register_1_memwrite_out), .MemRead(ex_mem_register_1_memread_out),
    .READ_DATA(data_memory_subsystem_1_read_data));
  mem_wb_register mem_wb_register_1 (
    .CLK(CLK), .reset(reset), .stall(stall), .flush(flush), .valid_in(ex_mem_register_1_valid_out),
    .pc_target_address_in(ex_mem_register_1_pc_target_address_out),
    .ALU_Result_in(ex_mem_register_1_alu_result_out), .rd_in(ex_mem_register_1_rd_out),
    .PC_in(ex_mem_register_1_pc_out), .immediate_in(ex_mem_register_1_immediate_out),
    .RegWrite_in(ex_mem_register_1_regwrite_out), .WritebackSel_in(ex_mem_register_1_writebacksel_out),
    .mem_read_data_in(data_memory_subsystem_1_read_data), .valid_out(mem_wb_register_1_valid_out),
    .pc_target_address_out(mem_wb_register_1_pc_target_address_out),
    .ALU_Result_out(mem_wb_register_1_alu_result_out), .rd_out(mem_wb_register_1_rd_out),
    .PC_out(mem_wb_register_1_pc_out), .immediate_out(mem_wb_register_1_immediate_out),
    .RegWrite_out(mem_wb_register_1_regwrite_out), .WritebackSel_out(mem_wb_register_1_writebacksel_out),
    .mem_read_data_out(mem_wb_register_1_mem_read_data_out));
  // NoConnect on mem_wb_register_1_pc_target_address_out
  writeback writeback_1 (
    .ALU_Result(mem_wb_register_1_alu_result_out), .PC(mem_wb_register_1_pc_out),
    .Memory_read_data(mem_wb_register_1_mem_read_data_out), .Immediate(mem_wb_register_1_immediate_out),
    .WritebackSel(mem_wb_register_1_writebacksel_out), .Writeback_data(writeback_1_writeback_data));

  // Other names for the same wires on the sheet: valid = valid_curr

  // Notes on the sheet:
  //   RegWrite
  //   Valid
  //   For later use pc_target_addr
endmodule

module instruction_fetch (
  input  CLK,
  input  reset,
  input  [31:0] next_pc,
  input  pc_write_enable_later,
  output [31:0] PC,
  output [31:0] Instruction,
  output [31:0] PC_plus_4
);

  Register #(.width(32)) PROGRAM_COUNTER (.D(next_pc), .en(1'b1), .clk(CLK), .Q(PC), .clr(reset));
  Adder #(.width(32)) adder_1 (.a(PC), .b(32'h4), .out(PC_plus_4));  // open: cin, cout
  instruction_memory_subsystem instruction_memory_subsystem_1 (.ADDRESS_CPU(PC), .READ_DATA(Instruction));

  // Other names for the same wires on the sheet: pc_write_enable = pc_write_enable_later
endmodule

module instruction_memory_subsystem (
  input  [31:0] ADDRESS_CPU,
  output [31:0] READ_DATA
);

  wire comparator_1_gt, memory_valid;
  wire [14:0] demultiplexer_1_out0, demultiplexer_1_out1;
  wire [31:0] RD1, RD2;

  Demultiplexer #(.width(15)) demultiplexer_1 (
    .out0(demultiplexer_1_out0), .out1(demultiplexer_1_out1), .in(ADDRESS_CPU[16:2]), .sel(ADDRESS_CPU[17]));
  Comparator #(.mode("unsigned"), .width(14)) comparator_1 (
    .a(ADDRESS_CPU[31:18]), .b({14{1'b0}}), .gt(comparator_1_gt));  // open: eq, lt
  not not_1 (memory_valid, comparator_1_gt);
  ROM #(.addrWidth(15), .dataWidth(32)) rom_1 (.addr(demultiplexer_1_out0), .data(RD1));
  ROM #(.addrWidth(15), .dataWidth(32)) rom_2 (.addr(demultiplexer_1_out1), .data(RD2));
  Multiplexer #(.width(32)) multiplexer_1 (.in0(RD1), .in1(RD2), .out(READ_DATA), .sel(ADDRESS_CPU[17]));

  // Other names for the same wires on the sheet: ADDRESS[14:0] = ADDRESS_CPU[16:2]; Module_sel_Bit = ADDRESS_CPU[17]

  // Notes on the sheet:
  //   contents of rom_1 (hex, n*v repeats v):
  //   500093 a00113 f00193
endmodule

module if_id_register (
  input  CLK,
  input  reset,
  input  flush,
  input  stall,
  input  valid_bit_in,
  input  [31:0] inst_in,
  input  [31:0] PC_in,
  output valid_bit_out,
  output [31:0] inst_out,
  output [31:0] PC_out
);

  wire not_1_out, not_2_out, not_3_out;

  not not_1 (not_1_out, stall);
  not not_2 (not_2_out, stall);
  not not_3 (not_3_out, stall);
  Register #(.width(1)) valid_reg (.D(valid_bit_in), .en(not_1_out), .clk(CLK), .Q(valid_bit_out), .clr(reset));
  Register #(.width(32)) Inst_reg (.D(inst_in), .en(not_2_out), .clk(CLK), .Q(inst_out), .clr(reset));
  Register #(.width(32)) PC_reg (.D(PC_in), .en(not_3_out), .clk(CLK), .Q(PC_out), .clr(reset));
endmodule

module instruction_decode (
  input  valid,
  input  [31:0] INSTRUCTION,
  output [2:0] func3,
  output [6:0] func7,
  output [4:0] rd,
  output [4:0] rs1,
  output [4:0] rs2,
  output [31:0] Immediate,
  output [1:0] ALUOp,
  output RegWrite,
  output [2:0] ImmSel,
  output MemWrite,
  output MemRead,
  output Jump,
  output I_type_JALR,
  output J_type_JAL,
  output Branch,
  output ALUSrc,
  output ALUSrcA,
  output [2:0] WritebackSel
);

  wire [6:0] instruction_splitter_1_opcode;

  instruction_splitter instruction_splitter_1 (
    .instruction(INSTRUCTION), .opcode(instruction_splitter_1_opcode), .rd(rd), .func3(func3), .rs1(rs1),
    .rs2(rs2), .func7(func7));
  main_control_unit main_control_unit_1 (
    .VALID(valid), .OPCODE(instruction_splitter_1_opcode), .ALUOp(ALUOp), .RegWrite(RegWrite),
    .ImmSel(ImmSel), .MemWrite(MemWrite), .MemRead(MemRead), .Jump(Jump), .I_type_JALR(I_type_JALR),
    .J_type_JAL(J_type_JAL), .Branch(Branch), .ALUSrc(ALUSrc), .WritebackSel(WritebackSel), .ALUSrcA(ALUSrcA));
  immediate_generator immediate_generator_1 (.INSTRUCTION_IN(INSTRUCTION), .Imm_Sel(ImmSel), .IMMEDIATE_OUT(Immediate));

  // Notes on the sheet:
  //   Instruction_metadata
  //   Control_Signals
endmodule

module register_file_subsystem (
  input  CLK,
  input  RESET,
  input  [4:0] ADDRESS_R_1,
  input  [4:0] ADDRESS_R_2,
  input  [4:0] ADDRESS_W_3,
  input  WRITE_ENABLE,
  input  [31:0] WRITE_DATA,
  output [31:0] READ_DATA_1,
  output [31:0] READ_DATA_2
);

  wire E0, E1, E2, E3, E4, E5, E6, E7, E8, E9, E10, E11, E12, E13, E14, E15, E16, E17, E18, E19, E20, E21,
       E22, E23, E24, E25, E26, E27, E28, E29, E30, E31, E32;
  wire [31:0] Q0, Q1, Q2, Q3, Q4, Q5, Q6, Q7, Q8, Q9, Q10, Q11, Q12, Q13, Q14, Q15, Q16, Q17, Q18, Q19, Q20,
       Q21, Q22, Q23, Q24, Q25, Q26, Q27, Q28, Q29, Q30, Q31;

  Register #(.width(32)) register_1 (.en(E0), .clk(CLK), .Q(Q0), .clr(1'b1));  // open: D
  Register #(.width(32)) register_2 (.D(WRITE_DATA), .en(E1), .clk(CLK), .Q(Q1), .clr(RESET));
  Register #(.width(32)) register_3 (.D(WRITE_DATA), .en(E2), .clk(CLK), .Q(Q2), .clr(RESET));
  Register #(.width(32)) register_4 (.D(WRITE_DATA), .en(E3), .clk(CLK), .Q(Q3), .clr(RESET));
  Decoder #(.select(5)) decoder_1 (
    .out0(E0), .out1(E1), .out2(E2), .out3(E3), .out4(E4), .out5(E5), .out6(E6), .out7(E7), .out8(E8),
    .out9(E9), .out10(E10), .out11(E11), .out12(E12), .out13(E13), .out14(E14), .out15(E15), .out16(E16),
    .out17(E17), .out18(E18), .out19(E19), .out20(E20), .out21(E21), .out22(E22), .out23(E23), .out24(E24),
    .out25(E25), .out26(E26), .out27(E27), .out28(E28), .out29(E29), .out30(E30), .out31(E31),
    .sel(ADDRESS_W_3), .en(WRITE_ENABLE));
  Register #(.width(32)) register_5 (.D(WRITE_DATA), .en(E5), .clk(CLK), .Q(Q4), .clr(RESET));
  Register #(.width(32)) register_6 (.D(WRITE_DATA), .en(E6), .clk(CLK), .Q(Q5), .clr(RESET));
  Register #(.width(32)) register_7 (.D(WRITE_DATA), .en(E7), .clk(CLK), .Q(Q6), .clr(RESET));
  Register #(.width(32)) register_8 (.D(WRITE_DATA), .en(E8), .clk(CLK), .Q(Q7), .clr(RESET));
  Multiplexer #(.select(5), .width(32)) multiplexer_1 (
    .in0(Q0), .in1(Q1), .in2(Q2), .in3(Q3), .in4(Q4), .in5(Q5), .in6(Q6), .in7(Q7), .in8(Q8), .in9(Q9),
    .in10(Q10), .in11(Q11), .in12(Q12), .in13(Q13), .in14(Q14), .in15(Q15), .in16(Q16), .in17(Q17),
    .in18(Q18), .in19(Q19), .in20(Q20), .in21(Q21), .in22(Q22), .in23(Q23), .in24(Q24), .in25(Q25),
    .in26(Q26), .in27(Q27), .in28(Q28), .in29(Q29), .in30(Q30), .in31(Q31), .out(READ_DATA_1),
    .sel(ADDRESS_R_1));
  Register #(.width(32)) register_9 (.D(WRITE_DATA), .en(E9), .clk(CLK), .Q(Q8), .clr(RESET));
  Register #(.width(32)) register_10 (.D(WRITE_DATA), .en(E10), .clk(CLK), .Q(Q9), .clr(RESET));
  Register #(.width(32)) register_11 (.D(WRITE_DATA), .en(E11), .clk(CLK), .Q(Q10), .clr(RESET));
  Register #(.width(32)) register_12 (.D(WRITE_DATA), .en(E12), .clk(CLK), .Q(Q11), .clr(RESET));
  Register #(.width(32)) register_13 (.D(WRITE_DATA), .en(E13), .clk(CLK), .Q(Q12), .clr(RESET));
  Register #(.width(32)) register_14 (.D(WRITE_DATA), .en(E14), .clk(CLK), .Q(Q13), .clr(RESET));
  Register #(.width(32)) register_15 (.D(WRITE_DATA), .en(E15), .clk(CLK), .Q(Q14), .clr(RESET));
  Register #(.width(32)) register_16 (.D(WRITE_DATA), .en(E16), .clk(CLK), .Q(Q15), .clr(RESET));
  Register #(.width(32)) register_17 (.D(WRITE_DATA), .en(E17), .clk(CLK), .Q(Q16), .clr(RESET));
  Register #(.width(32)) register_18 (.D(WRITE_DATA), .en(E18), .clk(CLK), .Q(Q17), .clr(RESET));
  Register #(.width(32)) register_19 (.D(WRITE_DATA), .en(E19), .clk(CLK), .Q(Q18), .clr(RESET));
  Register #(.width(32)) register_20 (.D(WRITE_DATA), .en(E20), .clk(CLK), .Q(Q19), .clr(RESET));
  Register #(.width(32)) register_21 (.D(WRITE_DATA), .en(E21), .clk(CLK), .Q(Q20), .clr(RESET));
  Register #(.width(32)) register_22 (.D(WRITE_DATA), .en(E22), .clk(CLK), .Q(Q21), .clr(RESET));
  Register #(.width(32)) register_23 (.D(WRITE_DATA), .en(E23), .clk(CLK), .Q(Q22), .clr(RESET));
  Register #(.width(32)) register_24 (.D(WRITE_DATA), .en(E24), .clk(CLK), .Q(Q23), .clr(RESET));
  Multiplexer #(.select(5), .width(32)) multiplexer_2 (
    .in0(Q0), .in1(Q1), .in2(Q2), .in3(Q3), .in4(Q4), .in5(Q5), .in6(Q6), .in7(Q7), .in8(Q8), .in9(Q9),
    .in10(Q10), .in11(Q11), .in12(Q12), .in13(Q13), .in14(Q14), .in15(Q15), .in16(Q16), .in17(Q17),
    .in18(Q18), .in19(Q19), .in20(Q20), .in21(Q21), .in22(Q22), .in23(Q23), .in24(Q24), .in25(Q25),
    .in26(Q26), .in27(Q27), .in28(Q28), .in29(Q29), .in30(Q30), .in31(Q31), .out(READ_DATA_2),
    .sel(ADDRESS_R_2));
  Register #(.width(32)) register_25 (.D(WRITE_DATA), .en(E25), .clk(CLK), .Q(Q24), .clr(RESET));
  Register #(.width(32)) register_26 (.D(WRITE_DATA), .en(E26), .clk(CLK), .Q(Q25), .clr(RESET));
  Register #(.width(32)) register_27 (.D(WRITE_DATA), .en(E27), .clk(CLK), .Q(Q26), .clr(RESET));
  Register #(.width(32)) register_28 (.D(WRITE_DATA), .en(E28), .clk(CLK), .Q(Q27), .clr(RESET));
  Register #(.width(32)) register_29 (.D(WRITE_DATA), .en(E29), .clk(CLK), .Q(Q28), .clr(RESET));
  Register #(.width(32)) register_30 (.D(WRITE_DATA), .en(E30), .clk(CLK), .Q(Q29), .clr(RESET));
  Register #(.width(32)) register_31 (.D(WRITE_DATA), .en(E31), .clk(CLK), .Q(Q30), .clr(RESET));
  Register #(.width(32)) register_32 (.D(WRITE_DATA), .en(E32), .clk(CLK), .Q(Q31), .clr(RESET));

  // Other names for the same wires on the sheet: WD[31:0] = WRITE_DATA; WE3 = WRITE_ENABLE
endmodule

module instruction_splitter (
  input  [31:0] instruction,
  output [6:0] opcode,
  output [4:0] rd,
  output [2:0] func3,
  output [4:0] rs1,
  output [4:0] rs2,
  output [6:0] func7
);


  assign func3 = instruction[14:12];
  assign func7 = instruction[31:25];
  assign opcode = instruction[6:0];
  assign rd = instruction[11:7];
  assign rs1 = instruction[19:15];
  assign rs2 = instruction[24:20];

  // Notes on the sheet:
  //   opcode
  //   func3
  //   func7
  //   rd
  //   rs1
  //   rs2
endmodule

module immediate_generator (
  input  [31:0] INSTRUCTION_IN,
  input  [2:0] Imm_Sel,
  output [31:0] IMMEDIATE_OUT
);

  wire [31:0] bit_extender_1_out, bit_extender_2_out, bit_extender_3_out, bit_extender_4_out;

  assign bit_extender_1_out = {{20{INSTRUCTION_IN[31]}}, INSTRUCTION_IN[31:20]};  // Bit_Extender bit_extender_1
  assign bit_extender_2_out = {{20{INSTRUCTION_IN[31]}}, {INSTRUCTION_IN[31:25], INSTRUCTION_IN[11:7]}};  // Bit_Extender bit_extender_2
  assign bit_extender_3_out = {{19{INSTRUCTION_IN[31]}}, {INSTRUCTION_IN[31], INSTRUCTION_IN[7], INSTRUCTION_IN[30:25], INSTRUCTION_IN[11:8], 1'b0}};  // Bit_Extender bit_extender_3
  assign bit_extender_4_out = {{11{INSTRUCTION_IN[31]}}, {INSTRUCTION_IN[31], INSTRUCTION_IN[19:12], INSTRUCTION_IN[20], INSTRUCTION_IN[30:21], 1'b0}};  // Bit_Extender bit_extender_4
  Multiplexer #(.select(3), .width(32)) multiplexer_1 (
    .in1(bit_extender_1_out), .in2(bit_extender_2_out), .in3(bit_extender_3_out),
    .in4({INSTRUCTION_IN[31:12], {12{1'b0}}}), .in5(bit_extender_4_out), .out(IMMEDIATE_OUT), .sel(Imm_Sel));  // open: in0, in6, in7

  // Other names for the same wires on the sheet: INSTRUCTION[31:0] = INSTRUCTION_IN

  // Notes on the sheet:
  //   I-Type
  //   S-Type
  //   B-Type
  //   U-Type
  //   J-Type
endmodule

module main_control_unit (
  input  VALID,
  input  [6:0] OPCODE,
  output [1:0] ALUOp,
  output RegWrite,
  output [2:0] ImmSel,
  output MemWrite,
  output MemRead,
  output Jump,
  output I_type_JALR,
  output J_type_JAL,
  output Branch,
  output ALUSrc,
  output [2:0] WritebackSel,
  output ALUSrcA
);

  wire I_type_MISC_MEM, I_type_OP_IMM, I_type_SYSTEM, or_4_out, or_5_out, or_6_out, or_7_out, or_8_out,
       R_type_OP, U_type_LUI;

  or or_1 (Jump, I_type_JALR, J_type_JAL);
  or or_2 (ALUSrc, MemRead, I_type_OP_IMM, ALUSrcA, MemWrite, U_type_LUI, I_type_JALR);
  or or_3 (RegWrite, R_type_OP, I_type_OP_IMM, MemRead, I_type_JALR, J_type_JAL, U_type_LUI, ALUSrcA);
  instruction_decoder instruction_decoder_1 (
    .OPCODE(OPCODE), .VALID(VALID), .I_type_LOAD(MemRead), .I_type_MISC_MEM(I_type_MISC_MEM),
    .I_type_OP_IMM(I_type_OP_IMM), .U_type_AUIPC(ALUSrcA), .S_type_STORE(MemWrite), .R_type_OP(R_type_OP),
    .U_type_LUI(U_type_LUI), .B_type_BRANCH(Branch), .I_type_JALR(I_type_JALR), .J_type_JAL(J_type_JAL),
    .I_type_SYSTEM(I_type_SYSTEM));
  or or_4 (or_4_out, MemRead, I_type_MISC_MEM, I_type_OP_IMM, I_type_JALR, I_type_SYSTEM);
  or or_5 (or_5_out, I_type_JALR, J_type_JAL);
  or or_6 (or_6_out, ALUSrcA, U_type_LUI);
  or or_7 (or_7_out, R_type_OP, ALUSrcA, I_type_OP_IMM);
  Priority_Encoder priority_encoder_1 (
    .in0(R_type_OP), .in1(or_4_out), .in2(MemWrite), .in3(Branch), .in4(or_6_out), .in5(J_type_JAL),
    .out(ImmSel), .en_in(VALID));  // open: in6, in7, gs, en_out
  Priority_Encoder priority_encoder_2 (
    .in0(or_7_out), .in1(MemRead), .in2(or_5_out), .in3(U_type_LUI), .out(WritebackSel), .en_in(VALID));  // open: in4, in5, in6, in7, gs, en_out
  or or_8 (or_8_out, ALUSrcA, U_type_LUI, I_type_JALR, J_type_JAL, MemRead, MemWrite);
  Priority_Encoder #(.select(2)) priority_encoder_3 (
    .in0(or_8_out), .in1(Branch), .in2(R_type_OP), .in3(I_type_OP_IMM), .out(ALUOp), .en_in(VALID));  // open: gs, en_out

  // Other names for the same wires on the sheet: B_type_BRANCH = Branch; I_type_LOAD = MemRead;
  //   S_type_STORE = MemWrite; U_type_AUIPC = ALUSrcA

  // Notes on the sheet:
  //   PC_PLUS_4
  //   ALU_RESULT
  //   MEMORY_DATA
  //   IMMEDIATE
  //   BRANCH_CLASS
  //   RTYPE_CLASS
  //   ITYPE_CLASS
  //   ADD_CLASS
endmodule

module instruction_decoder (
  input  [6:0] OPCODE,
  input  VALID,
  output I_type_LOAD,
  output I_type_MISC_MEM,
  output I_type_OP_IMM,
  output U_type_AUIPC,
  output S_type_STORE,
  output R_type_OP,
  output U_type_LUI,
  output B_type_BRANCH,
  output I_type_JALR,
  output J_type_JAL,
  output I_type_SYSTEM
);

  wire decoder_2_out0, decoder_2_out1, decoder_2_out3, demultiplexer_3_out1;

  Decoder decoder_1 (.sel(OPCODE[6]), .en(VALID));  // open: out0, out1
  Decoder #(.select(2)) decoder_2 (
    .out0(decoder_2_out0), .out1(decoder_2_out1), .out3(decoder_2_out3), .sel(OPCODE[6:5]), .en(VALID));  // open: out2
  Demultiplexer #(.enable("true"), .select(2)) demultiplexer_1 (
    .out0(I_type_LOAD), .out1(I_type_MISC_MEM), .out2(I_type_OP_IMM), .out3(U_type_AUIPC),
    .in(decoder_2_out0), .sel({OPCODE[4], OPCODE[2]}), .en(VALID));
  Demultiplexer #(.enable("true"), .select(2)) demultiplexer_2 (
    .out0(S_type_STORE), .out2(R_type_OP), .out3(U_type_LUI), .in(decoder_2_out1),
    .sel({OPCODE[4], OPCODE[2]}), .en(VALID));  // open: out1
  Demultiplexer #(.enable("true"), .select(2)) demultiplexer_3 (
    .out0(B_type_BRANCH), .out1(demultiplexer_3_out1), .out2(I_type_SYSTEM), .in(decoder_2_out3),
    .sel({OPCODE[4], OPCODE[2]}), .en(VALID));  // open: out3
  Demultiplexer #(.enable("true")) demultiplexer_4 (
    .out0(I_type_JALR), .out1(J_type_JAL), .in(demultiplexer_3_out1), .sel(OPCODE[3]), .en(VALID));

  // Other names for the same wires on the sheet: OPCD2_4bit[1:0] = {OPCODE[4], OPCODE[2]}; two = OPCODE[2];
  //   OPCD3bit = OPCODE[3]; three = OPCODE[3]; four = OPCODE[4]; five = OPCODE[5]; OPCD5_6bit[1:0] = OPCODE[6:5];
  //   six = OPCODE[6]
endmodule

module id_ex_register (
  input  CLK,
  input  reset,
  input  stall,
  input  flush,
  input  valid_in,
  input  [2:0] func3_in,
  input  [6:0] func7_in,
  input  [31:0] PC_in,
  input  [4:0] rd_in,
  input  [4:0] rs1_in,
  input  [4:0] rs2_in,
  input  [31:0] immediate_in,
  input  [1:0] ALUOp_in,
  input  RegWrite_in,
  input  [2:0] ImmSel_in,
  input  MemWrite_in,
  input  MemRead_in,
  input  Jump_in,
  input  I_TYEP_JALR_in,
  input  J_TYPE_JAL_in,
  input  Branch_in,
  input  ALUSrc_in,
  input  ALUSrcA_in,
  input  [2:0] WritebackSel_in,
  input  [31:0] rs1_data_in,
  input  [31:0] rs2_data_in,
  output valid_out,
  output [2:0] func3_out,
  output [6:0] func7_out,
  output [31:0] PC_out,
  output [4:0] rd_out,
  output [4:0] rs1_out,
  output [4:0] rs2_out,
  output [31:0] immediate_out,
  output [1:0] ALUOp_out,
  output RegWrite_out,
  output [2:0] ImmSel_out,
  output MemWrite_out,
  output MemRead_out,
  output Jump_out,
  output I_TYEP_JALR_out,
  output J_TYPE_JAL_out,
  output Branch_out,
  output ALUSrc_out,
  output ALUSrcA_out,
  output [2:0] WritebackSel_out,
  output [31:0] rs1_data_out,
  output [31:0] rs2_data_out
);

  wire not_1_out, not_2_out, not_3_out, not_4_out, not_5_out, not_6_out, not_7_out, not_8_out, not_9_out,
       not_10_out, not_11_out, not_12_out, not_13_out, not_14_out, not_15_out, not_16_out, not_17_out,
       not_18_out, not_19_out, not_20_out, not_21_out, not_22_out;

  not not_1 (not_1_out, stall);
  not not_2 (not_2_out, stall);
  not not_3 (not_3_out, stall);
  not not_4 (not_4_out, stall);
  not not_5 (not_5_out, stall);
  not not_6 (not_6_out, stall);
  Register #(.width(3)) func3_reg (.D(func3_in), .en(not_1_out), .clk(CLK), .Q(func3_out), .clr(reset));
  Register #(.width(2)) ALUOp_reg (.D(ALUOp_in), .en(not_3_out), .clk(CLK), .Q(ALUOp_out), .clr(reset));
  Register #(.width(1)) Jump_reg (.D(Jump_in), .en(not_4_out), .clk(CLK), .Q(Jump_out), .clr(reset));
  Register #(.width(3)) WritebackSel_reg (
    .D(WritebackSel_in), .en(not_5_out), .clk(CLK), .Q(WritebackSel_out), .clr(reset));
  Register #(.width(32)) rs1_data_reg (.D(rs1_data_in), .en(not_6_out), .clk(CLK), .Q(rs1_data_out), .clr(reset));
  Register #(.width(32)) immediate_reg (.D(immediate_in), .en(not_2_out), .clk(CLK), .Q(immediate_out), .clr(reset));
  not not_7 (not_7_out, stall);
  not not_8 (not_8_out, stall);
  not not_9 (not_9_out, stall);
  Register #(.width(1)) RegWrite_reg (.D(RegWrite_in), .en(not_8_out), .clk(CLK), .Q(RegWrite_out), .clr(reset));
  Register #(.width(1)) I_TYEP_JALR_reg (
    .D(I_TYEP_JALR_in), .en(not_9_out), .clk(CLK), .Q(I_TYEP_JALR_out), .clr(reset));
  not not_10 (not_10_out, stall);
  not not_11 (not_11_out, stall);
  Register #(.width(7)) func7_reg (.D(func7_in), .en(not_7_out), .clk(CLK), .Q(func7_out), .clr(reset));
  Register #(.width(32)) rs2_data_reg (.D(rs2_data_in), .en(not_10_out), .clk(CLK), .Q(rs2_data_out), .clr(reset));
  Register #(.width(1)) valid_reg (.D(valid_in), .en(not_11_out), .clk(CLK), .Q(valid_out), .clr(reset));
  not not_12 (not_12_out, stall);
  not not_13 (not_13_out, stall);
  not not_14 (not_14_out, stall);
  Register #(.width(32)) PC_reg (.D(PC_in), .en(not_12_out), .clk(CLK), .Q(PC_out), .clr(reset));
  Register #(.width(3)) ImmSel_reg (.D(ImmSel_in), .en(not_13_out), .clk(CLK), .Q(ImmSel_out), .clr(reset));
  Register #(.width(1)) J_TYPE_JAL_reg (.D(J_TYPE_JAL_in), .en(not_14_out), .clk(CLK), .Q(J_TYPE_JAL_out), .clr(reset));
  not not_15 (not_15_out, stall);
  Register #(.width(5)) rd_reg (.D(rd_in), .en(not_15_out), .clk(CLK), .Q(rd_out), .clr(reset));
  not not_16 (not_16_out, stall);
  not not_17 (not_17_out, stall);
  Register #(.width(1)) MemWrite_reg (.D(MemWrite_in), .en(not_16_out), .clk(CLK), .Q(MemWrite_out), .clr(reset));
  Register #(.width(1)) Branch_reg (.D(Branch_in), .en(not_17_out), .clk(CLK), .Q(Branch_out), .clr(reset));
  not not_18 (not_18_out, stall);
  Register #(.width(5)) rs1_reg (.D(rs1_in), .en(not_18_out), .clk(CLK), .Q(rs1_out), .clr(reset));
  not not_19 (not_19_out, stall);
  not not_20 (not_20_out, stall);
  Register #(.width(1)) MemRead_reg (.D(MemRead_in), .en(not_19_out), .clk(CLK), .Q(MemRead_out), .clr(reset));
  Register #(.width(1)) ALUSrc_reg (.D(ALUSrc_in), .en(not_20_out), .clk(CLK), .Q(ALUSrc_out), .clr(reset));
  not not_21 (not_21_out, stall);
  Register #(.width(5)) rs2_reg (.D(rs2_in), .en(not_21_out), .clk(CLK), .Q(rs2_out), .clr(reset));
  not not_22 (not_22_out, stall);
  Register #(.width(1)) ALUSrcA_reg (.D(ALUSrcA_in), .en(not_22_out), .clk(CLK), .Q(ALUSrcA_out), .clr(reset));

  // Notes on the sheet:
  //   Metadata_REGs
  //   Data_REGs
  //   Control_REGs
  //   Addres_REGs
endmodule

module execute (
  input  valid,
  input  [2:0] func3,
  input  [6:0] func7,
  input  [31:0] PC,
  input  [31:0] Immediate,
  input  [1:0] ALUOp,
  input  ALUSrc,
  input  ALUSrcA,
  input  I_TYEP_JALR,
  input  [31:0] rs1_data,
  input  [31:0] rs2_data,
  output [31:0] pc_target_address,
  output [31:0] ALU_Result,
  output branch_taken
);

  wire [3:0] alu_control_unit_1_alu_control;
  wire [31:0] Operand_A, Operand_B;

  pc_target_address_generator pc_target_address_generator_1 (
    .PC(PC), .rs1_data(rs1_data), .immediate(Immediate), .I_TYPE_JALR(I_TYEP_JALR),
    .pc_target_address(pc_target_address));
  operand_a_select_mux operand_a_select_mux_1 (.rs1_data(rs1_data), .PC(PC), .ALUSrcA(ALUSrcA), .Operand_A(Operand_A));
  operand_b_select_mux operand_b_select_mux_1 (
    .rs2_data(rs2_data), .Immediate(Immediate), .ALUSrc(ALUSrc), .Operand_B(Operand_B));
  alu_control_unit alu_control_unit_1 (
    .ALUOp(ALUOp), .func3(func3), .func7(func7), .valid(valid), .ALU_Control(alu_control_unit_1_alu_control));
  alu_subsystem alu_subsystem_1 (
    .func3(func3), .ALU_Control(alu_control_unit_1_alu_control), .Operand_A(Operand_A),
    .Operand_B(Operand_B), .valid(valid), .Result(ALU_Result), .branch_taken(branch_taken));
endmodule

module pc_target_address_generator (
  input  [31:0] PC,
  input  [31:0] rs1_data,
  input  [31:0] immediate,
  input  I_TYPE_JALR,
  output [31:0] pc_target_address
);

  wire [31:0] jalr_target, pc_relative_target;

  Adder #(.width(32)) adder_1 (.a(PC), .b(rs1_data), .out(jalr_target));  // open: cin, cout
  Adder #(.width(32)) adder_2 (.a(PC), .b(immediate), .out(pc_relative_target));  // open: cin, cout
  Multiplexer #(.width(32)) multiplexer_1 (
    .in0(pc_relative_target), .in1(jalr_target), .out(pc_target_address), .sel(I_TYPE_JALR));
endmodule

module pc_control_unit (
  input  branch_taken,
  input  I_TYPE_JALR,
  input  J_TYPE_JAL,
  input  B_TYPE_BRANCH,
  output take_control_flow
);

  wire branch_jump;

  and and_1 (branch_jump, branch_taken, B_TYPE_BRANCH);
  or or_1 (take_control_flow, branch_jump, J_TYPE_JAL, I_TYPE_JALR);
endmodule

module alu_control_unit (
  input  [1:0] ALUOp,
  input  [2:0] func3,
  input  [6:0] func7,
  input  valid,
  output [3:0] ALU_Control
);

  wire decoder_1_out0, decoder_1_out1, decoder_1_out2, decoder_1_out3, decoder_1_out4, decoder_1_out5,
       decoder_1_out6, decoder_1_out7, decoder_2_out0, decoder_2_out1, decoder_2_out2, decoder_2_out3,
       decoder_3_out1, decoder_3_out5, demultiplexer_1_out0, demultiplexer_1_out1, demultiplexer_2_out0,
       demultiplexer_2_out1, priority_encoder_2_p3, priority_encoder_2_p4, priority_encoder_2_p5,
       priority_encoder_2_p6, priority_encoder_2_p7, priority_encoder_2_p8, priority_encoder_2_p9,
       priority_encoder_2_p10, priority_encoder_2_p11;
  wire [3:0] ADD_CLASS_ALU_Ctrl, B_TYPE_ALU_Ctrl, I_TYPE_ALU_Ctrl, R_TYPE_ALU_Ctrl;

  Decoder #(.select(3)) decoder_1 (
    .out0(decoder_1_out0), .out1(decoder_1_out1), .out2(decoder_1_out2), .out3(decoder_1_out3),
    .out4(decoder_1_out4), .out5(decoder_1_out5), .out6(decoder_1_out6), .out7(decoder_1_out7), .sel(func3),
    .en(valid));
  Demultiplexer demultiplexer_1 (
    .out0(demultiplexer_1_out0), .out1(demultiplexer_1_out1), .in(decoder_1_out0), .sel(func7[5]));
  Demultiplexer demultiplexer_2 (
    .out0(demultiplexer_2_out0), .out1(demultiplexer_2_out1), .in(decoder_1_out5), .sel(func7[5]));
  Decoder #(.select(2)) decoder_2 (
    .out0(decoder_2_out0), .out1(decoder_2_out1), .out2(decoder_2_out2), .out3(decoder_2_out3), .sel(ALUOp),
    .en(valid));
  Multiplexer #(.width(4)) multiplexer_1 (.in1(4'b1010), .out(B_TYPE_ALU_Ctrl), .sel(decoder_2_out1));  // open: in0
  Priority_Encoder #(.select(4)) priority_encoder_1 (
    .in0(demultiplexer_1_out0), .in1(demultiplexer_1_out1), .in2(decoder_1_out7), .in3(decoder_1_out6),
    .in4(decoder_1_out4), .in5(decoder_1_out1), .in6(demultiplexer_2_out0), .in7(demultiplexer_2_out1),
    .in8(decoder_1_out2), .in9(decoder_1_out3), .out(R_TYPE_ALU_Ctrl), .en_in(decoder_2_out2));  // open: in10, in11, in12, in13, in14, in15, gs, en_out
  Multiplexer #(.select(2), .width(4)) multiplexer_2 (
    .in0(ADD_CLASS_ALU_Ctrl), .in1(B_TYPE_ALU_Ctrl), .in2(R_TYPE_ALU_Ctrl), .in3(I_TYPE_ALU_Ctrl),
    .out(ALU_Control), .sel(ALUOp));
  // Priority_Encoder #(.select(4)) priority_encoder_2: pin names not known; wires that end beside it: I_TYPE_ALU_Ctrl, decoder_2_out3, priority_encoder_2_p3, priority_encoder_2_p4, priority_encoder_2_p5, priority_encoder_2_p6, priority_encoder_2_p7, priority_encoder_2_p8, priority_encoder_2_p9, priority_encoder_2_p10, priority_encoder_2_p11
  Multiplexer #(.width(4)) multiplexer_3 (.in1(4'b0000), .out(ADD_CLASS_ALU_Ctrl), .sel(decoder_2_out0));  // open: in0
  Demultiplexer demultiplexer_3 (.out0(priority_encoder_2_p7), .in(decoder_3_out1), .sel(func7[5]));  // open: out1
  Demultiplexer demultiplexer_4 (
    .out0(priority_encoder_2_p8), .out1(priority_encoder_2_p9), .in(decoder_3_out5), .sel(func7[5]));
  Decoder #(.select(3)) decoder_3 (
    .out0(priority_encoder_2_p3), .out1(decoder_3_out1), .out2(priority_encoder_2_p10),
    .out3(priority_encoder_2_p11), .out4(priority_encoder_2_p6), .out5(decoder_3_out5),
    .out6(priority_encoder_2_p5), .out7(priority_encoder_2_p4), .sel(func3), .en(valid));

  // Other names for the same wires on the sheet: func7_bit5 = func7[5]

  // Notes on the sheet:
  //   R_TYPE
  //   BRANCH_TYPE
  //   ADD_CLASS
  //   I_TYPE
endmodule

module alu_subsystem (
  input  [2:0] func3,
  input  [3:0] ALU_Control,
  input  [31:0] Operand_A,
  input  [31:0] Operand_B,
  input  valid,
  output [31:0] Result,
  output branch_taken
);

  wire comparator_1_eq;
  wire [31:0] adder_subunit_1_result_add, adder_subunit_1_result_sub, compare_subunit_1_signed_less_than,
       compare_subunit_1_unsigned_less_than, logic_subunit_1_result_and, logic_subunit_1_result_or,
       logic_subunit_1_result_xor, shift_subunit_1_result_sll, shift_subunit_1_result_sra,
       shift_subunit_1_result_srl, undriven;

  Comparator #(.width(4)) comparator_1 (.a(ALU_Control), .b(4'b1010), .eq(comparator_1_eq));  // open: gt, lt
  adder_subunit adder_subunit_1 (
    .Operand_A(Operand_A), .Operand_B(Operand_B), .Result_ADD(adder_subunit_1_result_add),
    .Result_SUB(adder_subunit_1_result_sub));
  logic_subunit logic_subunit_1 (
    .Operand_A(Operand_A), .Operand_B(Operand_B), .Result_AND(logic_subunit_1_result_and),
    .Result_OR(logic_subunit_1_result_or), .Result_XOR(logic_subunit_1_result_xor));
  shift_subunit shift_subunit_1 (
    .Operand_A(Operand_A), .Operand_B(Operand_B), .Result_SLL(shift_subunit_1_result_sll),
    .Result_SRL(shift_subunit_1_result_srl), .Result_SRA(shift_subunit_1_result_sra));
  compare_subunit compare_subunit_1 (
    .Operand_A(Operand_A), .Operand_B(Operand_B), .signed_less_than(compare_subunit_1_signed_less_than),
    .unsigned_less_than(compare_subunit_1_unsigned_less_than));
  branch_comparator branch_comparator_1 (
    .Operand_A(Operand_A), .Operand_B(Operand_B), .func3(func3), .branch_enable(comparator_1_eq),
    .valid(valid), .branch_taken(branch_taken));
  // NoConnect on undriven
  Multiplexer #(.select(4), .width(32)) multiplexer_1 (
    .in0(adder_subunit_1_result_add), .in1(adder_subunit_1_result_sub), .in2(logic_subunit_1_result_and),
    .in3(logic_subunit_1_result_or), .in4(logic_subunit_1_result_xor), .in5(shift_subunit_1_result_sll),
    .in6(shift_subunit_1_result_srl), .in7(shift_subunit_1_result_sra),
    .in8(compare_subunit_1_signed_less_than), .in9(compare_subunit_1_unsigned_less_than), .in10(undriven),
    .out(Result), .sel(ALU_Control));  // open: in11, in12, in13, in14, in15

  // Notes on the sheet:
  //   Check if ALU_Control == 1010
  //   Separate_Branch_Logic
  //   ALU_Control 1010 reserved for branch
endmodule

module adder_subunit (
  input  [31:0] Operand_A,
  input  [31:0] Operand_B,
  output [31:0] Result_ADD,
  output [31:0] Result_SUB
);

  Adder #(.width(32)) adder_1 (.a(Operand_A), .b(Operand_B), .out(Result_ADD));  // open: cin, cout
  Subtractor #(.width(32)) subtractor_1 (.a(Operand_A), .b(Operand_B), .out(Result_SUB));  // open: bin, bout
endmodule

module logic_subunit (
  input  [31:0] Operand_A,
  input  [31:0] Operand_B,
  output [31:0] Result_AND,
  output [31:0] Result_OR,
  output [31:0] Result_XOR
);

  assign Result_AND = Operand_A & Operand_B;  // AND_Gate and_1, 32 bits wide
  assign Result_OR = Operand_A | Operand_B;  // OR_Gate or_1, 32 bits wide
  assign Result_XOR = Operand_A ^ Operand_B;  // XOR_Gate xor_1, 32 bits wide
endmodule

module shift_subunit (
  input  [31:0] Operand_A,
  input  [31:0] Operand_B,
  output [31:0] Result_SLL,
  output [31:0] Result_SRL,
  output [31:0] Result_SRA
);

  Shifter #(.width(32)) shifter_1 (.in(Operand_A), .\dist (Operand_B[4:0]), .out(Result_SLL));
  Shifter #(.shift("lr"), .width(32)) shifter_2 (.in(Operand_A), .\dist (Operand_B[4:0]), .out(Result_SRL));
  Shifter #(.shift("ar"), .width(32)) shifter_3 (.in(Operand_A), .\dist (Operand_B[4:0]), .out(Result_SRA));
endmodule

module compare_subunit (
  input  [31:0] Operand_A,
  input  [31:0] Operand_B,
  output [31:0] signed_less_than,
  output [31:0] unsigned_less_than
);

  wire signed_less_than_t, unsigned_less_than_t;

  Comparator #(.width(32)) comparator_1 (.a(Operand_A), .b(Operand_B), .lt(signed_less_than_t));  // open: gt, eq
  Comparator #(.mode("unsigned"), .width(32)) comparator_2 (
    .a(Operand_A), .b(Operand_B), .lt(unsigned_less_than_t));  // open: gt, eq
  assign signed_less_than = {{31{1'b0}}, signed_less_than_t};  // Bit_Extender bit_extender_1
  assign unsigned_less_than = {{31{1'b0}}, unsigned_less_than_t};  // Bit_Extender bit_extender_2

  // Notes on the sheet:
  //   Signed
  //   Unsigned
endmodule

module branch_comparator (
  input  [31:0] Operand_A,
  input  [31:0] Operand_B,
  input  [2:0] func3,
  input  branch_enable,
  input  valid,
  output branch_taken
);

  wire comparator_1_eq, comparator_2_gt, comparator_2_lt, comparator_3_lt, comparator_4_eq, comparator_4_gt,
       comparator_5_lt, comparator_6_eq, comparator_6_gt, multiplexer_1_out, or_1_out, or_2_out, or_3_out;

  Comparator #(.width(32)) comparator_1 (.a(Operand_A), .b(Operand_B), .eq(comparator_1_eq));  // open: gt, lt
  or or_1 (or_1_out, comparator_2_gt, comparator_2_lt);
  Comparator #(.width(32)) comparator_2 (
    .a(Operand_A), .b(Operand_B), .gt(comparator_2_gt), .lt(comparator_2_lt));  // open: eq
  Comparator #(.width(32)) comparator_3 (.a(Operand_A), .b(Operand_B), .lt(comparator_3_lt));  // open: gt, eq
  or or_2 (or_2_out, comparator_4_gt, comparator_4_eq);
  Comparator #(.width(32)) comparator_4 (
    .a(Operand_A), .b(Operand_B), .gt(comparator_4_gt), .eq(comparator_4_eq));  // open: lt
  Comparator #(.mode("unsigned"), .width(32)) comparator_5 (
    .a(Operand_A), .b(Operand_B), .lt(comparator_5_lt));  // open: gt, eq
  Comparator #(.mode("unsigned"), .width(32)) comparator_6 (
    .a(Operand_A), .b(Operand_B), .gt(comparator_6_gt), .eq(comparator_6_eq));  // open: lt
  or or_3 (or_3_out, comparator_6_gt, comparator_6_eq);
  Multiplexer #(.enable("true"), .select(3)) multiplexer_1 (
    .in0(comparator_1_eq), .in1(or_1_out), .in4(comparator_3_lt), .in5(or_2_out), .in6(comparator_5_lt),
    .in7(or_3_out), .out(multiplexer_1_out), .sel(func3), .en(valid));  // open: in2, in3
  and and_1 (branch_taken, branch_enable, multiplexer_1_out);

  // Notes on the sheet:
  //   signed_greater_than_equal
  //   unsigned_less_than
  //   unsigned_greater_than_equal
  //   equal
  //   not_equal
  //   signed_less_than
endmodule

module operand_a_select_mux (
  input  [31:0] rs1_data,
  input  [31:0] PC,
  input  ALUSrcA,
  output [31:0] Operand_A
);

  Multiplexer #(.width(32)) multiplexer_1 (.in0(rs1_data), .in1(PC), .out(Operand_A), .sel(ALUSrcA));
endmodule

module operand_b_select_mux (
  input  [31:0] rs2_data,
  input  [31:0] Immediate,
  input  ALUSrc,
  output [31:0] Operand_B
);

  Multiplexer #(.width(32)) multiplexer_1 (.in0(rs2_data), .in1(Immediate), .out(Operand_B), .sel(ALUSrc));
endmodule

module ex_mem_register (
  input  CLK,
  input  reset,
  input  stall,
  input  flush,
  input  valid_in,
  input  [31:0] pc_target_address_in,
  input  [31:0] ALU_Result_in,
  input  branch_taken_in,
  input  [4:0] rd_in,
  input  [31:0] PC_in,
  input  [31:0] immediate_in,
  input  RegWrite_in,
  input  MemWrite_in,
  input  MemRead_in,
  input  [2:0] WritebackSel_in,
  input  [31:0] rs2_data_in,
  output valid_out,
  output [31:0] pc_target_address_out,
  output [31:0] ALU_Result_out,
  output branch_taken_out,
  output [4:0] rd_out,
  output [31:0] PC_out,
  output [31:0] immediate_out,
  output RegWrite_out,
  output MemWrite_out,
  output MemRead_out,
  output [2:0] WritebackSel_out,
  output [31:0] rs2_data_out
);

  wire not_1_out, not_2_out, not_3_out, not_4_out, not_5_out, not_6_out, not_7_out, not_8_out, not_9_out,
       not_10_out, not_11_out, not_12_out;

  not not_1 (not_1_out, stall);
  not not_2 (not_2_out, stall);
  not not_3 (not_3_out, stall);
  not not_4 (not_4_out, stall);
  Register #(.width(32)) ALU_Result_reg (.D(ALU_Result_in), .en(not_1_out), .clk(CLK), .Q(ALU_Result_out), .clr(reset));
  Register #(.width(5)) rd_reg (.D(rd_in), .en(not_2_out), .clk(CLK), .Q(rd_out), .clr(reset));
  Register #(.width(1)) RegWrite_reg (.D(RegWrite_in), .en(not_3_out), .clk(CLK), .Q(RegWrite_out), .clr(reset));
  Register #(.width(3)) WritebackSel_reg (
    .D(WritebackSel_in), .en(not_4_out), .clk(CLK), .Q(WritebackSel_out), .clr(reset));
  not not_5 (not_5_out, stall);
  not not_6 (not_6_out, stall);
  not not_7 (not_7_out, stall);
  Register #(.width(32)) PC_reg (.D(PC_in), .en(not_5_out), .clk(CLK), .Q(PC_out), .clr(reset));
  not not_8 (not_8_out, stall);
  not not_9 (not_9_out, stall);
  Register #(.width(1)) branch_taken_reg (
    .D(branch_taken_in), .en(not_7_out), .clk(CLK), .Q(branch_taken_out), .clr(reset));
  Register #(.width(1)) MemWrite_reg (.D(MemWrite_in), .en(not_6_out), .clk(CLK), .Q(MemWrite_out), .clr(reset));
  Register #(.width(32)) rs2_data_reg (.D(rs2_data_in), .en(not_8_out), .clk(CLK), .Q(rs2_data_out), .clr(reset));
  Register #(.width(1)) valid_reg (.D(valid_in), .en(not_9_out), .clk(CLK), .Q(valid_out), .clr(reset));
  not not_10 (not_10_out, stall);
  not not_11 (not_11_out, stall);
  Register #(.width(32)) immediate_reg (.D(immediate_in), .en(not_10_out), .clk(CLK), .Q(immediate_out), .clr(reset));
  Register #(.width(1)) MemRead_reg (.D(MemRead_in), .en(not_11_out), .clk(CLK), .Q(MemRead_out), .clr(reset));
  not not_12 (not_12_out, stall);
  Register #(.width(32)) pc_target_address_reg (
    .D(pc_target_address_in), .en(not_12_out), .clk(CLK), .Q(pc_target_address_out), .clr(reset));
endmodule

module data_memory_subsystem (
  input  CLK,
  input  [31:0] ADDRESS_CPU,
  input  [31:0] WRITE_DATA,
  input  MemWrite,
  input  MemRead,
  output [31:0] READ_DATA
);

  wire comparator_1_gt, memory_valid, MemRead_t, MemWrite_t;
  wire [14:0] demultiplexer_1_out0, demultiplexer_1_out1;
  wire [31:0] RD1, RD2;

  and and_1 (MemWrite_t, memory_valid, MemWrite);
  and and_2 (MemRead_t, memory_valid, MemRead);
  Demultiplexer #(.width(15)) demultiplexer_1 (
    .out0(demultiplexer_1_out0), .out1(demultiplexer_1_out1), .in(ADDRESS_CPU[16:2]), .sel(ADDRESS_CPU[17]));
  not not_1 (memory_valid, comparator_1_gt);
  Comparator #(.mode("unsigned"), .width(14)) comparator_1 (
    .a(ADDRESS_CPU[31:18]), .b({14{1'b0}}), .gt(comparator_1_gt));  // open: eq, lt
  RAM #(.addrWidth(15), .asyncread("true"), .dataWidth(32)) ram_1 (
    .addr(demultiplexer_1_out0), .we(MemWrite_t), .oe(MemRead_t), .clk(CLK), .din(WRITE_DATA), .dout(RD1));
  RAM #(.addrWidth(15), .asyncread("true"), .dataWidth(32)) ram_2 (
    .addr(demultiplexer_1_out1), .we(MemWrite_t), .oe(MemRead_t), .clk(CLK), .din(WRITE_DATA), .dout(RD2));
  Multiplexer #(.width(32)) multiplexer_1 (.in0(RD1), .in1(RD2), .out(READ_DATA), .sel(ADDRESS_CPU[17]));

  // Other names for the same wires on the sheet: ADDRESS[14:0] = ADDRESS_CPU[16:2]; Module_sel_Bit = ADDRESS_CPU[17]
endmodule

module mem_wb_register (
  input  CLK,
  input  reset,
  input  stall,
  input  flush,
  input  valid_in,
  input  [31:0] pc_target_address_in,
  input  [31:0] ALU_Result_in,
  input  [4:0] rd_in,
  input  [31:0] PC_in,
  input  [31:0] immediate_in,
  input  RegWrite_in,
  input  [2:0] WritebackSel_in,
  input  [31:0] mem_read_data_in,
  output valid_out,
  output [31:0] pc_target_address_out,
  output [31:0] ALU_Result_out,
  output [4:0] rd_out,
  output [31:0] PC_out,
  output [31:0] immediate_out,
  output RegWrite_out,
  output [2:0] WritebackSel_out,
  output [31:0] mem_read_data_out
);

  wire not_1_out, not_2_out, not_3_out, not_4_out, not_5_out, not_6_out, not_7_out, not_8_out, not_9_out;

  not not_1 (not_1_out, stall);
  not not_2 (not_2_out, stall);
  not not_3 (not_3_out, stall);
  Register #(.width(32)) ALU_Result_reg (.D(ALU_Result_in), .en(not_1_out), .clk(CLK), .Q(ALU_Result_out), .clr(reset));
  not not_4 (not_4_out, stall);
  Register #(.width(1)) valid_reg (.D(valid_in), .en(not_3_out), .clk(CLK), .Q(valid_out), .clr(reset));
  Register #(.width(3)) WritebackSel_reg (
    .D(WritebackSel_in), .en(not_2_out), .clk(CLK), .Q(WritebackSel_out), .clr(reset));
  Register #(.width(32)) immediate_reg (.D(immediate_in), .en(not_4_out), .clk(CLK), .Q(immediate_out), .clr(reset));
  not not_5 (not_5_out, stall);
  not not_6 (not_6_out, stall);
  Register #(.width(5)) rd_reg (.D(rd_in), .en(not_6_out), .clk(CLK), .Q(rd_out), .clr(reset));
  not not_7 (not_7_out, stall);
  Register #(.width(32)) pc_target_address_reg (
    .D(pc_target_address_in), .en(not_5_out), .clk(CLK), .Q(pc_target_address_out), .clr(reset));
  not not_8 (not_8_out, stall);
  Register #(.width(32)) mem_read_data_reg (
    .D(mem_read_data_in), .en(not_7_out), .clk(CLK), .Q(mem_read_data_out), .clr(reset));
  not not_9 (not_9_out, stall);
  Register #(.width(1)) RegWrite_reg (.D(RegWrite_in), .en(not_8_out), .clk(CLK), .Q(RegWrite_out), .clr(reset));
  Register #(.width(32)) PC_reg (.D(PC_in), .en(not_9_out), .clk(CLK), .Q(PC_out), .clr(reset));
endmodule

module writeback (
  input  [31:0] ALU_Result,
  input  [31:0] PC,
  input  [31:0] Memory_read_data,
  input  [31:0] Immediate,
  input  [2:0] WritebackSel,
  output [31:0] Writeback_data
);

  wire [31:0] adder_1_out;

  Adder #(.width(32)) adder_1 (.a(PC), .b(32'h4), .out(adder_1_out));  // open: cin, cout
  Multiplexer #(.select(3), .width(32)) multiplexer_1 (
    .in0(ALU_Result), .in1(Memory_read_data), .in2(adder_1_out), .in3(Immediate), .out(Writeback_data),
    .sel(WritebackSel));  // open: in4, in5, in6, in7
endmodule
